// Logisim project solutions_of_adder.circ as structural Verilog: 3 circuits, main circuit full_addr_1bit
module full_addr_1bit (
  input  CI,
  input  B,
  input  A,
  output CO,
  output SUM
);

  wire and_1_out, and_2_out, and_3_out, and_4_out, and_5_out, xnor_1_out, xor_1_out;

  and and_1 (and_1_out, ~CI, B, A);  // AND_Gate
  and and_2 (and_2_out, CI, A);
  and and_3 (and_3_out, CI, B, ~A);  // AND_Gate
  or or_1 (CO, and_1_out, and_2_out, and_3_out);
  xor xor_1 (xor_1_out, CI, A);
  and and_4 (and_4_out, xor_1_out, ~B);  // AND_Gate
  or or_2 (SUM, and_4_out, and_5_out);
  xnor xnor_1 (xnor_1_out, CI, A);
  and and_5 (and_5_out, xnor_1_out, B);
endmodule

module full_addr_1bit_m2 (
  input  CI,
  input  B,
  input  A,
  output CO,
  output SUM
);

  wire and_1_out, and_2_out, xor_2_out;

  xor xor_1 (SUM, CI, xor_2_out);
  xor xor_2 (xor_2_out, B, A);
  and and_1 (and_1_out, xor_2_out, CI);
  or or_1 (CO, and_1_out, and_2_out);
  and and_2 (and_2_out, B, A);
endmodule

module full_addr_4bit (
  input  [3:0] B,
  input  [3:0] A,
  output S4,
  output S3,
  output S2,
  output S1,
  output S0
);

  wire full_addr_1bit_m2_2_co, full_addr_1bit_m2_3_co, full_addr_1bit_m2_4_co;

  full_addr_1bit_m2 full_addr_1bit_m2_1 (.CI(full_addr_1bit_m2_2_co), .B(B[3]), .A(A[3]), .SUM(S3), .CO(S4));
  full_addr_1bit_m2 full_addr_1bit_m2_2 (
    .CI(full_addr_1bit_m2_3_co), .B(B[2]), .A(A[2]), .SUM(S2), .CO(full_addr_1bit_m2_2_co));
  full_addr_1bit_m2 full_addr_1bit_m2_3 (
    .CI(full_addr_1bit_m2_4_co), .B(B[1]), .A(A[1]), .SUM(S1), .CO(full_addr_1bit_m2_3_co));
  full_addr_1bit_m2 full_addr_1bit_m2_4 (.CI(1'b0), .B(B[0]), .A(A[0]), .SUM(S0), .CO(full_addr_1bit_m2_4_co));
endmodule
